// Logisim project 8-bit Register file.circ as structural Verilog: 1 circuit, main circuit main
module main (
  input  clk,
  input  [15:0] WriteData,
  input  [2:0] Read_register_1__rs,
  input  [2:0] Write_Register,
  input  [2:0] Read_register_2__rt,
  input  RegWrite,
  output [15:0] Read_data_1,
  output [15:0] Read_data_2
);

  wire and_1_out, and_2_out, and_3_out, and_4_out, and_5_out, and_6_out, and_7_out, and_8_out,
       decoder_1_out0, decoder_1_out1, decoder_1_out2, decoder_1_out3, decoder_1_out4, decoder_1_out5,
       decoder_1_out6, decoder_1_out7;
  wire [15:0] _0_q, _1_q, _2_q, _3_q, _4_q, _5_q, _6_q, _7_q;

  Decoder #(.select(3)) decoder_1 (
    .out0(decoder_1_out0), .out1(decoder_1_out1), .out2(decoder_1_out2), .out3(decoder_1_out3),
    .out4(decoder_1_out4), .out5(decoder_1_out5), .out6(decoder_1_out6), .out7(decoder_1_out7),
    .sel(Write_Register));  // open: en
  and and_1 (and_1_out, decoder_1_out0, RegWrite);
  and and_2 (and_2_out, decoder_1_out1, RegWrite);
  and and_3 (and_3_out, decoder_1_out2, RegWrite);
  and and_4 (and_4_out, decoder_1_out3, RegWrite);
  and and_5 (and_5_out, decoder_1_out4, RegWrite);
  and and_6 (and_6_out, decoder_1_out5, RegWrite);
  and and_7 (and_7_out, decoder_1_out6, RegWrite);
  and and_8 (and_8_out, decoder_1_out7, RegWrite);
  Register #(.width(16)) _0 (.D(WriteData), .en(and_1_out), .Q(_0_q), .clk(clk));  // open: clr
  Register #(.width(16)) _1 (.D(WriteData), .en(and_2_out), .Q(_1_q), .clk(clk));  // open: clr
  Register #(.width(16)) _2 (.D(WriteData), .en(and_3_out), .Q(_2_q), .clk(clk));  // open: clr
  Register #(.width(16)) _3 (.D(WriteData), .en(and_4_out), .Q(_3_q), .clk(clk));  // open: clr
  Register #(.width(16)) _4 (.D(WriteData), .en(and_5_out), .Q(_4_q), .clk(clk));  // open: clr
  Register #(.width(16)) _5 (.D(WriteData), .en(and_6_out), .Q(_5_q), .clk(clk));  // open: clr
  Register #(.width(16)) _6 (.D(WriteData), .en(and_7_out), .Q(_6_q), .clk(clk));  // open: clr
  Register #(.width(16)) _7 (.D(WriteData), .en(and_8_out), .Q(_7_q), .clk(clk));  // open: clr
  Multiplexer #(.select(3), .width(16)) multiplexer_1 (
    .in0(_0_q), .in1(_1_q), .in2(_2_q), .in3(_3_q), .in4(_4_q), .in5(_5_q), .in6(_6_q), .in7(_7_q),
    .out(Read_data_1), .sel(Read_register_1__rs));  // open: en
  Multiplexer #(.select(3), .width(16)) multiplexer_2 (
    .in0(_0_q), .in1(_1_q), .in2(_2_q), .in3(_3_q), .in4(_4_q), .in5(_5_q), .in6(_6_q), .in7(_7_q),
    .out(Read_data_2), .sel(Read_register_2__rt));  // open: en
endmodule
