// Logisim project ALU control.circ as structural Verilog: 1 circuit, main circuit main
module main (
  input  [1:0] ALUop,
  input  [3:0] Funct,
  output [3:0] ALU_control
);

  wire and_2_out;

  and and_1 (ALU_control[0], Funct[0], ALUop[1]);
  or or_1 (ALU_control[1], ~ALUop[1], ~Funct[2]);  // OR_Gate
  or or_2 (ALU_control[2], ALUop[0], and_2_out);
  and and_2 (and_2_out, ALUop[1], Funct[1]);

  assign ALU_control[3] = 1'b0;
endmodule
