// Logisim project CPU-16-bit.circ as structural Verilog: 1 circuit, main circuit main
module main (
  input  Cin,
  input  reset,
  output Zero,
  output [15:0] out_4,
  output [15:0] out_5,
  output [3:0] ALU_control
);

  wire and_1_out, CLK_out, main_2_alu_src, main_2_branch, main_2_jump, main_2_mem_read, main_2_mem_write,
       main_2_memtoreg, main_2_regdst, main_2_regwrite, n16_bit_alu_1_overflow;
  wire [1:0] main_2_aluop;
  wire [2:0] multiplexer_1_out;
  wire [15:0] adder_1_out, adder_2_out, bit_extender_1_out, main_1_jump, main_3_read_data_1,
       multiplexer_2_out, multiplexer_3_out, multiplexer_4_out, n16_bit_alu_1_result, ram_1_data,
       register_1_q, rom_1_data;

  Register #(.width(16)) register_1 (.D(multiplexer_4_out), .Q(register_1_q), .clk(CLK_out), .clr(reset));  // open: en
  Clock CLK (.out(CLK_out));
  Adder #(.width(16)) adder_1 (.a(register_1_q), .b(16'h1), .out(adder_1_out), .cin(Cin));  // open: cout
  ROM #(.addrWidth(16), .dataWidth(16)) rom_1 (.addr(register_1_q), .data(rom_1_data));  // open: sel
  jump_main main_1 (.PC(adder_1_out), .Instruction(rom_1_data), .jump(main_1_jump));
  Control_unit_main main_2 (
    .OPCode(rom_1_data[15:13]), .RegDst(main_2_regdst), .RegWrite(main_2_regwrite), .ALU_SRC(main_2_alu_src),
    .Mem_Read(main_2_mem_read), .Mem_Write(main_2_mem_write), .MemToReg(main_2_memtoreg),
    .Branch(main_2_branch), .Jump(main_2_jump), .ALUop(main_2_aluop));
  Multiplexer #(.width(3), .enable("false")) multiplexer_1 (
    .in0(rom_1_data[9:7]), .in1(rom_1_data[6:4]), .out(multiplexer_1_out), .sel(main_2_regdst));
  _8_bit_Register_file_main main_3 (
    .WriteData(out_5), .Write_Register(multiplexer_1_out), .RegWrite(main_2_regwrite),
    .Read_data_1(main_3_read_data_1), .Read_register_1__rs(rom_1_data[12:10]), .Read_data_2(out_4),
    .Read_register_2__rt(rom_1_data[9:7]), .clk(CLK_out));
  assign bit_extender_1_out = {{9{rom_1_data[6]}}, rom_1_data[6:0]};  // Bit_Extender bit_extender_1
  Multiplexer #(.width(16), .enable("false")) multiplexer_2 (
    .in0(out_4), .in1(bit_extender_1_out), .out(multiplexer_2_out), .sel(main_2_alu_src));
  Adder #(.width(16)) adder_2 (.a(adder_1_out), .b(bit_extender_1_out), .out(adder_2_out));  // open: cin, cout
  and and_1 (and_1_out, main_2_branch, Zero);
  _16_bit_alu u_16_bit_alu_1 (
    .B(multiplexer_2_out), .A(main_3_read_data_1), .ALU_Op(ALU_control[1:0]), .result(n16_bit_alu_1_result),
    .zero(Zero), .Overflow(n16_bit_alu_1_overflow), .B_Inv(ALU_control[2]), .Cin(ALU_control[2]));
  ALU_control_main main_4 (.ALUop(main_2_aluop), .Funct(rom_1_data[3:0]), .ALU_control(ALU_control));
  Multiplexer #(.width(16), .enable("false")) multiplexer_3 (
    .in0(adder_1_out), .in1(adder_2_out), .out(multiplexer_3_out), .sel(and_1_out));
  Multiplexer #(.width(16), .enable("false")) multiplexer_4 (
    .in0(multiplexer_3_out), .in1(main_1_jump), .out(multiplexer_4_out), .sel(main_2_jump));
  RAM #(.addrWidth(16), .dataWidth(16), .bus("separate")) ram_1 (
    .addr(n16_bit_alu_1_result), .din(out_4), .data(ram_1_data), .str(main_2_mem_write), .clk(CLK_out),
    .ld(main_2_mem_read));  // open: sel, clr
  Multiplexer #(.width(16)) multiplexer_5 (
    .in0(n16_bit_alu_1_result), .in1(ram_1_data), .out(out_5), .sel(main_2_memtoreg));  // open: en

  // Notes on the sheet:
  //   001 ->lw
  //   010 -> sw
  //   011 -> beq
  //   100 -> jump
  //   00 -> AND
  //   01-> OR
  //   OPcode
  //   000 -> R-trype
  //   ALU control bit (R-type)
  //   10 -> Add, Sub
  //   funct
  //   contents of rom_1 (hex, n*v repeats v):
  //   530 532 2584 4584 6580 8002 8eaf
  //   opcode
endmodule
