// Logisim project Control-unit.circ as structural Verilog: 1 circuit, main circuit main
module main (
  input  [2:0] OPCode,
  output RegDst,
  output RegWrite,
  output ALU_SRC,
  output Mem_Read,
  output Mem_Write,
  output MemToReg,
  output Branch,
  output Jump,
  output [1:0] ALUop
);

  wire not_1_out, not_2_out, not_3_out, not_4_out, not_5_out, not_6_out, not_7_out, not_8_out, not_9_out,
       not_10_out;

  not not_1 (not_1_out, OPCode[2]);
  not not_2 (not_2_out, OPCode[1]);
  and R_type (ALUop[1], not_1_out, not_2_out, not_3_out);
  not not_3 (not_3_out, OPCode[0]);
  not not_4 (not_4_out, OPCode[2]);
  not not_5 (not_5_out, OPCode[1]);
  and LW (Mem_Read, not_4_out, not_5_out, OPCode[0]);
  not not_6 (not_6_out, OPCode[2]);
  not not_7 (not_7_out, OPCode[0]);
  not not_8 (not_8_out, OPCode[2]);
  and SW (Mem_Write, not_6_out, OPCode[1], not_7_out);
  and Beq (ALUop[0], not_8_out, OPCode[1], OPCode[0]);
  not not_9 (not_9_out, OPCode[0]);
  not not_10 (not_10_out, OPCode[1]);
  and u_Jump (Jump, OPCode[2], not_10_out, not_9_out);
  or or_1 (RegWrite, ALUop[1], Mem_Read);
  or or_2 (ALU_SRC, Mem_Read, Mem_Write);

  assign Branch = ALUop[0];
  assign MemToReg = Mem_Read;
  assign RegDst = ALUop[1];
endmodule
