// Logisim project alu-16-bit.circ as structural Verilog: 2 circuits, main circuit main
module main (
  input  A,
  input  B,
  input  Cin,
  input  [2:0] ALU_OP,
  input  B_Inv,
  output Result,
  output Cout
);

  wire adder_1_out, and_1_out, multiplexer_1_out, nand_1_out, nor_1_out, not_1_out, or_1_out;

  not not_1 (not_1_out, B);
  Multiplexer multiplexer_1 (.in0(B), .in1(not_1_out), .out(multiplexer_1_out), .sel(B_Inv));  // open: en
  and and_1 (and_1_out, A, B);
  or or_1 (or_1_out, A, B);
  nor nor_1 (nor_1_out, A, B);
  nand nand_1 (nand_1_out, A, B);
  Adder #(.width(1)) adder_1 (.a(A), .b(multiplexer_1_out), .out(adder_1_out), .cin(Cin), .cout(Cout));
  Multiplexer #(.select(3)) multiplexer_2 (
    .in0(and_1_out), .in1(or_1_out), .in2(nor_1_out), .in3(nand_1_out), .in4(adder_1_out), .out(Result),
    .sel(ALU_OP));  // open: in5, in6, in7, en
endmodule

module _16_bit_alu (
  input  B_Inv,
  input  Cin,
  input  [15:0] B,
  input  [15:0] A,
  input  [2:0] ALU_Op,
  output [15:0] Result,
  output Zero,
  output Overflow
);

  wire main_1_cout, main_2_cout, main_3_cout, main_4_cout, main_5_cout, main_6_cout, main_7_cout,
       main_8_cout, main_9_cout, main_10_cout, main_11_cout, main_12_cout, main_13_cout, main_14_cout,
       main_15_cout, main_16_cout;

  main main_1 (.B_Inv(B_Inv), .Result(Result[0]), .ALU_OP(ALU_Op), .Cout(main_1_cout), .A(A[0]), .B(B[0]), .Cin(Cin));
  main main_2 (
    .B_Inv(B_Inv), .Result(Result[1]), .ALU_OP(ALU_Op), .Cout(main_2_cout), .A(A[1]), .B(B[1]),
    .Cin(main_1_cout));
  main main_3 (
    .B_Inv(B_Inv), .Result(Result[2]), .ALU_OP(ALU_Op), .Cout(main_3_cout), .A(A[2]), .B(B[2]),
    .Cin(main_2_cout));
  main main_4 (
    .B_Inv(B_Inv), .Result(Result[3]), .ALU_OP(ALU_Op), .Cout(main_4_cout), .A(A[3]), .B(B[3]),
    .Cin(main_3_cout));
  main main_5 (
    .B_Inv(B_Inv), .Result(Result[4]), .ALU_OP(ALU_Op), .Cout(main_5_cout), .A(A[4]), .B(B[4]),
    .Cin(main_4_cout));
  main main_6 (
    .B_Inv(B_Inv), .Result(Result[5]), .ALU_OP(ALU_Op), .Cout(main_6_cout), .A(A[5]), .B(B[5]),
    .Cin(main_5_cout));
  main main_7 (
    .B_Inv(B_Inv), .Result(Result[6]), .ALU_OP(ALU_Op), .Cout(main_7_cout), .A(A[6]), .B(B[6]),
    .Cin(main_6_cout));
  main main_8 (
    .B_Inv(B_Inv), .Result(Result[7]), .ALU_OP(ALU_Op), .Cout(main_8_cout), .A(A[7]), .B(B[7]),
    .Cin(main_7_cout));
  main main_9 (
    .B_Inv(B_Inv), .Result(Result[8]), .ALU_OP(ALU_Op), .Cout(main_9_cout), .A(A[8]), .B(B[8]),
    .Cin(main_8_cout));
  main main_10 (
    .B_Inv(B_Inv), .Result(Result[9]), .ALU_OP(ALU_Op), .Cout(main_10_cout), .A(A[9]), .B(B[9]),
    .Cin(main_9_cout));
  main main_11 (
    .B_Inv(B_Inv), .Result(Result[10]), .ALU_OP(ALU_Op), .Cout(main_11_cout), .A(A[10]), .B(B[10]),
    .Cin(main_10_cout));
  main main_12 (
    .B_Inv(B_Inv), .Result(Result[11]), .ALU_OP(ALU_Op), .Cout(main_12_cout), .A(A[11]), .B(B[11]),
    .Cin(main_11_cout));
  main main_13 (
    .B_Inv(B_Inv), .Result(Result[12]), .ALU_OP(ALU_Op), .Cout(main_13_cout), .A(A[12]), .B(B[12]),
    .Cin(main_12_cout));
  main main_14 (
    .B_Inv(B_Inv), .Result(Result[13]), .ALU_OP(ALU_Op), .Cout(main_14_cout), .A(A[13]), .B(B[13]),
    .Cin(main_13_cout));
  main main_15 (
    .B_Inv(B_Inv), .Result(Result[14]), .ALU_OP(ALU_Op), .Cout(main_15_cout), .A(A[14]), .B(B[14]),
    .Cin(main_14_cout));
  main main_16 (
    .B_Inv(B_Inv), .Result(Result[15]), .ALU_OP(ALU_Op), .Cout(main_16_cout), .A(A[15]), .B(B[15]),
    .Cin(main_15_cout));
  xor xor_1 (Overflow, main_15_cout, main_16_cout);
  nor nor_1 (Zero, Result[0], Result[1], Result[2], Result[3], Result[4], Result[5], Result[6], Result[7], Result[8], Result[9], Result[10], Result[11], Result[12], Result[13], Result[14], Result[15]);
endmodule
