// Logisim project jump.circ as structural Verilog: 1 circuit, main circuit main
module main (
  input  [15:0] PC,
  input  [15:0] Instruction,
  output [15:0] jump
);


  assign jump = {PC[15:13], Instruction[12:0]};
endmodule
