// Logisim project lubba-CPU-16-bit.circ as structural Verilog: 1 circuit, main circuit main
module main (
  input  Cin,
  output out_2,
  output [15:0] out_3,
  output [15:0] out_4,
  output [3:0] out_5
);

  wire and_1_out, CLK_out, main_1_alu_src, main_1_branch, main_1_jump, main_1_mem_read, main_1_mem_write,
       main_1_memtoreg, main_1_regdst, main_1_regwrite;
  wire [1:0] main_1_aluop;
  wire [2:0] multiplexer_1_out;
  wire [15:0] adder_1_out, adder_2_out, bit_extender_1_out, jump_1_p3, main_2_read_data_1, multiplexer_2_out,
       multiplexer_3_out, multiplexer_4_out, n16_bit_alu_1_result, PC_q, ram_1_data, rom_1_data;

  Register #(.width(16)) PC (.D(multiplexer_4_out), .Q(PC_q), .clk(CLK_out));  // open: en, clr
  Clock CLK (.out(CLK_out));
  Adder #(.width(16)) adder_1 (.a(PC_q), .b(16'h1), .out(adder_1_out), .cin(Cin));  // open: cout
  ROM #(.addrWidth(16), .dataWidth(16)) rom_1 (.addr(PC_q), .data(rom_1_data));  // open: sel
  // jump jump_1: pin names not known; wires that end beside it: adder_1_out, rom_1_data, jump_1_p3
  Control_unit_main main_1 (
    .OPCode(rom_1_data[15:13]), .RegDst(main_1_regdst), .RegWrite(main_1_regwrite), .ALU_SRC(main_1_alu_src),
    .Mem_Read(main_1_mem_read), .Mem_Write(main_1_mem_write), .MemToReg(main_1_memtoreg),
    .Branch(main_1_branch), .Jump(main_1_jump), .ALUop(main_1_aluop));
  Multiplexer #(.width(3)) multiplexer_1 (
    .in0(rom_1_data[9:7]), .in1(rom_1_data[6:4]), .out(multiplexer_1_out), .sel(main_1_regdst));  // open: en
  _8_bit_Register_file_main main_2 (
    .WriteData(out_4), .Write_Register(multiplexer_1_out), .RegWrite(main_1_regwrite),
    .Read_data_1(main_2_read_data_1), .Read_register_1__rs(rom_1_data[12:10]), .Read_data_2(out_3),
    .Read_register_2__rt(rom_1_data[9:7]), .clk(CLK_out));
  assign bit_extender_1_out = {{9{rom_1_data[6]}}, rom_1_data[6:0]};  // Bit_Extender bit_extender_1
  Multiplexer #(.width(16)) multiplexer_2 (
    .in0(out_3), .in1(bit_extender_1_out), .out(multiplexer_2_out), .sel(main_1_alu_src));  // open: en
  Adder #(.width(16)) adder_2 (.a(adder_1_out), .b(bit_extender_1_out), .out(adder_2_out));  // open: cin, cout
  and and_1 (and_1_out, main_1_branch, out_2);
  _16_bit_alu u_16_bit_alu_1 (
    .B(multiplexer_2_out), .A(main_2_read_data_1), .ALU_Op(out_5[1:0]), .result(n16_bit_alu_1_result),
    .zero(out_2), .B_Inv(out_5[2]), .Cin(out_5[2]));  // open: Overflow
  ALU_control_main main_3 (.ALUop(main_1_aluop), .Funct(rom_1_data[3:0]), .ALU_control(out_5));
  Multiplexer #(.width(16)) multiplexer_3 (
    .in0(adder_1_out), .in1(adder_2_out), .out(multiplexer_3_out), .sel(and_1_out));  // open: en
  Multiplexer #(.width(16)) multiplexer_4 (
    .in0(multiplexer_3_out), .in1(jump_1_p3), .out(multiplexer_4_out), .sel(main_1_jump));  // open: en
  RAM #(.addrWidth(16), .dataWidth(16), .bus("separate")) ram_1 (
    .addr(n16_bit_alu_1_result), .din(out_3), .data(ram_1_data), .str(main_1_mem_write), .clk(CLK_out),
    .ld(main_1_mem_read));  // open: sel, clr
  Multiplexer #(.width(16)) multiplexer_5 (
    .in0(n16_bit_alu_1_result), .in1(ram_1_data), .out(out_4), .sel(main_1_memtoreg));  // open: en

  // Notes on the sheet:
  //   funct
  //   opcode
endmodule
